// Logisim project Синхронный вычитающий счетчик с параллельным переносом.circ as structural Verilog: 1 circuit, main circuit main
module main (
);

  wire and_1_out, and_2_out, nand_1_out, nand_2_out, nand_3_out, nand_4_out, nand_5_out, nand_6_out,
       nand_7_out, nand_9_out, nand_10_out, nand_11_out, nand_12_out, nand_13_out, nand_14_out, nand_16_out,
       nand_17_out, nand_18_out, nand_19_out, nand_20_out, nand_21_out, nand_22_out, nand_24_out,
       nand_25_out, nand_26_out, nand_27_out, nand_28_out, nand_29_out, nand_30_out, nand_32_out, not_1_out,
       not_2_out, not_3_out, not_4_out, not_5_out, or_1_out, reset_out, x1_1_out;
  wire [3:0] nand_8_out;

  Button reset (.out(reset_out));
  Clock x1_1 (.out(x1_1_out));
  not not_1 (not_1_out, reset_out);
  nand nand_1 (nand_1_out, nand_8_out[0], or_1_out, x1_1_out);
  nand nand_2 (nand_2_out, x1_1_out, or_1_out, nand_7_out);
  nand nand_3 (nand_3_out, nand_4_out, not_2_out);
  nand nand_4 (nand_4_out, not_1_out, nand_1_out, nand_6_out);
  nand nand_5 (nand_5_out, nand_6_out, not_2_out);
  nand nand_6 (nand_6_out, nand_4_out, nand_2_out);
  not not_2 (not_2_out, x1_1_out);
  nand nand_7 (nand_7_out, not_1_out, nand_3_out, nand_8_out[0]);
  nand nand_8 (nand_8_out[0], nand_7_out, nand_5_out);
  LED Q0 (.in(nand_8_out[0]));
  nand nand_9 (nand_9_out, nand_16_out, nand_7_out, x1_1_out);
  nand nand_10 (nand_10_out, x1_1_out, nand_7_out, nand_8_out[1]);
  nand nand_11 (nand_11_out, not_1_out, nand_9_out, nand_12_out);
  nand nand_12 (nand_12_out, nand_11_out, nand_10_out);
  not not_3 (not_3_out, x1_1_out);
  nand nand_13 (nand_13_out, nand_11_out, not_3_out);
  nand nand_14 (nand_14_out, nand_12_out, not_3_out);
  nand nand_15 (nand_8_out[1], not_1_out, nand_13_out, nand_16_out);
  nand nand_16 (nand_16_out, nand_8_out[1], nand_14_out);
  LED Q1 (.in(nand_8_out[1]));
  and and_1 (and_1_out, nand_16_out, nand_7_out);
  nand nand_17 (nand_17_out, nand_24_out, and_1_out, x1_1_out);
  nand nand_18 (nand_18_out, x1_1_out, and_1_out, nand_8_out[2]);
  nand nand_19 (nand_19_out, not_1_out, nand_17_out, nand_20_out);
  nand nand_20 (nand_20_out, nand_19_out, nand_18_out);
  not not_4 (not_4_out, x1_1_out);
  nand nand_21 (nand_21_out, nand_19_out, not_4_out);
  nand nand_22 (nand_22_out, nand_20_out, not_4_out);
  LED Q2 (.in(nand_8_out[2]));
  nand nand_23 (nand_8_out[2], not_1_out, nand_21_out, nand_24_out);
  nand nand_24 (nand_24_out, nand_8_out[2], nand_22_out);
  and and_2 (and_2_out, nand_24_out, and_1_out);
  nand nand_25 (nand_25_out, nand_32_out, and_2_out, x1_1_out);
  nand nand_26 (nand_26_out, x1_1_out, and_2_out, nand_8_out[3]);
  nand nand_27 (nand_27_out, not_1_out, nand_25_out, nand_28_out);
  nand nand_28 (nand_28_out, nand_27_out, nand_26_out);
  not not_5 (not_5_out, x1_1_out);
  nand nand_29 (nand_29_out, nand_27_out, not_5_out);
  nand nand_30 (nand_30_out, nand_28_out, not_5_out);
  Hex_Digit_Display hex_digit_display_1 (.value(nand_8_out));  // open: dp
  LED Q3 (.in(nand_8_out[3]));
  nand nand_31 (nand_8_out[3], not_1_out, nand_29_out, nand_32_out);
  nand nand_32 (nand_32_out, nand_8_out[3], nand_30_out);
  or or_1 (or_1_out, nand_8_out[0], nand_8_out[3], nand_8_out[1], nand_8_out[2]);
endmodule
